# Fritzing sketch Sensores (saved by Fritzing 0.9.9b)
breadboards: 1

parts:
  Componente1 = FC-28 Soil Hygrometer Module
  Componente2 = FC-28 Soil Hygrometer Module - Probe
  Componente3 = Adafruit T-Cobbler Plus [part_number="Adafruit #1989 and #2028"]
  DHT1 = DHT11 Humitidy and Temperature Sensor (3 pins)
  Componente4 = Adafruit ADS1115 16Bit I2C ADC [part_number="Adafruit #1085"]
  PART1 = ML8511 UV Sensor Breakout [part_number=SEN-12705]

nets:
  VCC: Componente1.VCC, Componente3.+5V, Componente4.VDD
  GND: Componente1.GND, Componente1.DO, Componente3.GND, Componente3.RXD, Componente3.GPIO18, Componente3.GPIO23, Componente3.GPIO24, Componente3.CE0, Componente3.CE1, Componente3.EECLK, Componente3.GPIO12, DHT1.GND, PART1.GND
  N1: Componente1.POS, Componente2.POS
  N2: Componente1.NEG, Componente2.NEG
  +3.3V: Componente3.+3.3V, DHT1.VDD, Componente4.AIN1, PART1.EN, PART1.3.3V
  N3: Componente3.SDA, Componente4.SDA
  N4: Componente3.SCL, Componente4.SCL
  N5: Componente3.GPIO4, DHT1.DATA

custom parts:
  FC-28 Soil Hygrometer Module: The FC-28 is a soil hygrometer module that uses the Texas Instruments LM393 comparator chip to provide an analog measurement of soil humidity. The digital output is high when soil moisture is over a certain threshold, as determined by adjusting the potentiometer.
  FC-28 Soil Hygrometer Module - Probe: The FC-28 is a soil hygrometer module that uses the Texas Instruments LM393 comparator chip to provide an analog measurement of soil humidity.
  Adafruit T-Cobbler Plus: The Raspberry Pi has landed on the Maker World like a 40-GPIO pinned, quad-USB ported, credit card sized bomb of DIY joy. And while you can use most of our great Model B accessories by hooking up our downgrade cable, its probably a good time to upgrade your set up and accessorize using all of the 40 pins. That's why we now carry the Assembled Adafruit Pi T-Cobbler Plus - Breakout + Cable for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
  DHT11 Humitidy and Temperature Sensor (3 pins): DHT11 Humidity and Temperature Sensor (3 pins) from the design created by John De Cristofaro for Adafruit Industries.
  Adafruit ADS1115 16Bit I2C ADC: For microcontrollers without an analog-to-digital converter or when you want a higher-precision ADC, the ADS1115 provides 16-bit precision at 860 samples/second over I2C. The chip can be configured as 4 single-ended input channels, or two differential channels. As a nice bonus, it even includes a programmable gain amplifier, up to x16, to help boost up smaller single/differential signals to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
  ML8511 UV Sensor Breakout: Description: The ML8511 breakout is an easy to use ultraviolet light sensor. The MP8511 UV Sensor works by outputing an analog signal in relation to the amount of UV light it detects. This breakout can be very handy in creating devices that warn the user of sunburn or detect the UV index as it relates to weather conditions. This sensor breakout can detect 280-390nm light most effectively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
